# Fritzing sketch tenzov2 (saved by Fritzing 0.9.3b)
circuit board: 8.46667cm x 5.64444cm
breadboards: 1

parts:
  Part1 = Bluetooth Mate Silver
  GY1 = MPU-6050 Board GY-521 [form="♀ (female)" package=THT]
  GPS1 = Adafruit Ultimate GPS Breakout
  Tiny_RTC1 = Tiny RTC
  SdModule1 = SdModule
  Part2 = Arduino Mega 2560 (Rev3)
  J1 = Dagu DGServo 9g header connector (female) [package=THT]
  J2 = Dagu DGServo 9g header connector (female) [package=THT]
  J3 = Dagu DGServo 9g header connector (female) [package=THT]
  J4 = Dagu DGServo 9g header connector (female) [package=THT]
  JP1 = Header 4 [package=1x04-1mm-ra]

nets:
  GND: Part1.RTS_5V, GY1.pin2, GPS1.GND, Tiny_RTC1.GND, SdModule1.GND, Part2.GND, J1.pulse, J2.pulse, J3.pulse, J4.pulse, JP1.1
  5V: Part1.RX_5V, GY1.pin1, GPS1.VIN, Tiny_RTC1.VCC, SdModule1.5V, Part2.5V, JP1.2
  N1: Part1.VCC, Part2.D19/RX1
  N2: Part1.CTS_5V, Part2.D18/TX1
  N3: GY1.pin3, Tiny_RTC1.SCL, Part2.D21/SCL, JP1.3
  N4: GY1.pin4, Tiny_RTC1.SDA, Part2.D20/SDA, JP1.4
  N5: GPS1.TX, Part2.D14/TX3
  N6: GPS1.RX, Part2.D15/RX3
  N7: SdModule1.SCK, Part2.D52
  N8: SdModule1.SS, Part2.D53
  N9: SdModule1.MISO, Part2.D50
  N10: SdModule1.MOSI, Part2.D51
  N11: Part2.D2_PWM, J3.gnd
  N12: Part2.D6_PWM, J1.gnd
  N13: Part2.D7_PWM, J4.gnd

custom parts:
  MPU-6050 Board GY-521: Acelerometro y Giroscopio MPU-6050 Board GY-521
  Tiny RTC: Tiny RTC I2C module DS1370Z RTC and AT24C32 EEPROM
